# Fritzing sketch MOO_Chan_Geki_Oshi (saved by Fritzing 1.0.2b)
breadboards: 1

parts:
  K4017 = Basic FET N-Channel [package="TO220 [THT]"]
  Turn_Table = DC Motor [voltage_(max)=6V voltage_(min)=3V]
  R1 = Resistor [tolerance=±5% power=0.25W resistance=1k package=THT]
  Arduino = Arduino Uno (Rev3)
  WS2812B = Dagu DGServo 9g header (male) [package=THT]
  R3 = Resistor [tolerance=±5% power=0.25W resistance=330 package=THT]
  R2 = Resistor [tolerance=±5% power=0.25W resistance=1k package=THT]

nets:
  N1: K4017.gate, R1.Pin_1, R2.Pin_0
  N2: K4017.drain, Turn_Table.pin_2
  GND: K4017.source, Arduino.GND, WS2812B.gnd, R2.Pin_1
  1.5V: Turn_Table.pin_1
  N3: R1.Pin_0, Arduino.D13/SCK
  N4: Arduino.D7, R3.Pin_0
  5V: Arduino.5V
  6V: WS2812B.Vcc
  N5: WS2812B.pulse, R3.Pin_1
